# Fritzing sketch Cablage fritzing (saved by Fritzing 0.9.2b)
breadboards: 1

parts:
  Arduino_NANO = Arduino Nano (Rev3.0)
  Interrupteur_1 = Power plug
  Relay_1 = KY-019 5V Relay Module [package="Breakout board"]
  Interrupteur_2 = Power plug
  Part1 = KY-019 5V Relay Module [package="Breakout board"]
  BT2 = Bluetooth HC-06u [package=THT]

nets:
  N1: Arduino_NANO.D1/TX, BT2.RXD
  N2: Arduino_NANO.D0/RX, BT2.TXD
  GND: Arduino_NANO.GND, Relay_1.-, Part1.-, BT2.GND
  5V: Arduino_NANO.5V, Relay_1.+, Part1.+, BT2.VCC
  N3: Arduino_NANO.A1, Part1.S
  N4: Arduino_NANO.A0, Relay_1.S
  N5: Interrupteur_1.VCC, Relay_1.NC
  N6: Interrupteur_1.GND, Relay_1.Common
  N7: Interrupteur_2.VCC, Part1.NC
  N8: Interrupteur_2.GND, Part1.Common

custom parts:
  KY-019 5V Relay Module: KY-019 5V Relay module, used to control AC circuits.
  Bluetooth HC-06u: Bluetooth HC-06 - face up, pins down 16.5mm x 37.5mm PCB
